# Fritzing sketch Arduino Pro Nano V3 to Ra-01 (SX1278) (saved by Fritzing 0.9.3b)

parts:
  LoRa_Module1 = Semtech [part_number=SX1278]
  Part1 = Arduino Nano (Rev3.0)

nets:
  N1: LoRa_Module1.connector2, Part1.D8
  N2: LoRa_Module1.connector3, Part1.D11/MOSI
  N3: LoRa_Module1.connector4, Part1.D12/MISO
  N4: LoRa_Module1.connector5, Part1.D13/SCK
  N5: LoRa_Module1.connector10, Part1.GND
  N6: LoRa_Module1.connector11, Part1.3V3
  N7: LoRa_Module1.connector12, Part1.D3
  N8: LoRa_Module1.connector13, Part1.D2

notes:
  BangGood Ra-01 (SX1278) Use only 3.3V
  NSS=CS (in SPI)
